// Logisim project class03.circ as structural Verilog: 1 circuit, main circuit main
module main (
  input  A,
  input  B,
  input  C,
  output S
);

  wire AND01_out, AND02_out, AND03_out, AND04_out, AND05_out, AND06_out, AND07_out, AND08_out, NOT_A_out,
       NOT_B_out, NOT_C_out, OR01_out, OR02_out, OR03_out;

  not NOT_A (NOT_A_out, A);
  not NOT_B (NOT_B_out, B);
  and AND01 (AND01_out, NOT_A_out, NOT_B_out);
  not NOT_C (NOT_C_out, C);
  and AND06 (AND06_out, A, B);
  and AND03 (AND03_out, AND01_out, C);
  and AND02 (AND02_out, AND01_out, NOT_C_out);
  and AND04 (AND04_out, NOT_B_out, NOT_C_out);
  and AND07 (AND07_out, AND06_out, NOT_C_out);
  and AND08 (AND08_out, AND06_out, C);
  or OR01 (OR01_out, AND03_out, AND02_out);
  and AND05 (AND05_out, A, AND04_out);
  or OR02 (OR02_out, OR01_out, AND05_out);
  or OR03 (OR03_out, OR02_out, AND07_out);
  or OR04 (S, OR03_out, AND08_out);

  // Notes on the sheet:
  //   class03: ~A~B~C+~A~BC+A~B~C+AB~C+ABC
endmodule
