// Logisim project truthtable.circ as structural Verilog: 1 circuit, main circuit minterms
module minterms (
  input  A,
  input  B,
  input  C,
  input  A_2,
  input  B_2,
  input  C_2,
  output S,
  output S_2
);

  wire and_1_out, and_2_out, and_3_out, and_4_out, and_5_out, and_6_out, and_7_out, not_1_out, not_2_out,
       not_3_out, not_4_out, not_5_out, not_6_out, or_1_out, or_2_out, or_3_out, or_4_out, or_5_out,
       or_6_out, or_7_out;

  not not_1 (not_1_out, A);
  not not_2 (not_2_out, A_2);
  not not_3 (not_3_out, B);
  not not_4 (not_4_out, B_2);
  not not_5 (not_5_out, C);
  not not_6 (not_6_out, C_2);
  and and_1 (and_1_out, not_1_out, B);
  and and_2 (and_2_out, A, not_3_out);
  and and_3 (and_3_out, A, not_3_out);
  or or_1 (or_1_out, A_2, B_2);
  or or_2 (or_2_out, not_2_out, B_2);
  or or_3 (or_3_out, not_2_out, not_4_out);
  and and_4 (and_4_out, and_1_out, not_5_out);
  and and_5 (and_5_out, and_2_out, not_5_out);
  and and_6 (and_6_out, and_3_out, C);
  or or_4 (or_4_out, or_1_out, not_6_out);
  or or_5 (or_5_out, or_2_out, not_6_out);
  or or_6 (or_6_out, or_3_out, C_2);
  or or_7 (or_7_out, and_4_out, and_5_out);
  and and_7 (and_7_out, or_4_out, or_5_out);
  or or_8 (S, or_7_out, and_6_out);
  and and_8 (S_2, and_7_out, or_6_out);

  // Notes on the sheet:
  //   S = (A'BC')+(AB'C')+(AB'C)
  //   S = (A+B+C')(A'+B+C')(A'+B'+C)
  //   minterms
  //   Maxterms
endmodule
